# Fritzing sketch proposed_sketch (saved by Fritzing 0.9.2b)
breadboards: 1

parts:
  Parte1 = Arduino Uno (Rev3)
  RE1 = Rotary Encoder [package=THT]
  LED1 = LED - 5mm [color="Red (633nm)" package="5 mm [THT]"]
  LED2 = LED - 5mm [color="Red (633nm)" package="5 mm [THT]"]
  R1 = Resistor [tolerance=±5% resistance=330 power=250mW package=THT]
  R2 = Resistor [tolerance=±5% resistance=330 power=250mW package=THT]
  R3 = Resistor [tolerance=±5% resistance=330 power=250mW package=THT]
  R4 = Resistor [tolerance=±5% resistance=330 power=250mW package=THT]
  R5 = Resistor [tolerance=±5% resistance=330 power=250mW package=THT]
  R6 = Resistor [tolerance=±5% resistance=10k package=THT]
  R7 = Resistor [tolerance=±5% resistance=330 power=250mW package=THT]
  R8 = Resistor [tolerance=±5% resistance=330 power=250mW package=THT]
  R9 = Resistor [tolerance=±5% resistance=1k package=THT]
  RE2 = Rotary Encoder [package=THT]
  J1 = double row male pin header, 2 pins [form="♂ (male)"]

nets:
  N1: Parte1.A0, RE2.EncoderPinC
  N2: Parte1.D11_PWM/MOSI, R7.Pin_1
  N3: Parte1.D12/MISO, R8.Pin_1
  N4: Parte1.D2, R1.Pin_1
  N5: Parte1.D3_PWM, R2.Pin_1
  N6: Parte1.D4, R3.Pin_1
  N7: Parte1.D5_PWM, R4.Pin_1
  N8: Parte1.D6_PWM, R5.Pin_1
  N9: Parte1.5V, RE2.EncoderPinB
  N10: Parte1.GND, RE1.EncoderPinA, LED1.cathode, LED2.cathode, R9.Pin_0, RE2.EncoderPinA, J1.pin1
  N11: RE1.EncoderPinC, J1.pin2
  N12: RE1.EncoderPinB, R6.Pin_0
  N13: LED1.anode, R8.Pin_0
  N14: LED2.anode, R7.Pin_0
  N15: R1.Pin_0, R2.Pin_0, R3.Pin_0, R4.Pin_0, R5.Pin_0, R6.Pin_1

notes:
  Mono audio output
  Volume
  Tempo
