# Fritzing sketch arduitunes_jack (saved by Fritzing 0.8.7b)
circuit board: 8.46667cm x 5.64444cm
breadboards: 1

parts:
  Parte1 = Arduino Uno (Rev3)
  R1 = Resistor [tolerance=±10% resistance=330 package=THT]
  R4 = Resistor [tolerance=±5% resistance=330 package=THT]
  R5 = Resistor [tolerance=±5% resistance=330 package=THT]
  R3 = Resistor [tolerance=±5% resistance=330 package=THT]
  R6 = Resistor [tolerance=±5% resistance=330 package=THT]
  LED1 = LED - 5mm [color="Red (633nm)" package="5 mm [THT]"]
  LED2 = LED - 5mm [color="Blue (470nm)" package="5 mm [THT]"]
  R7 = Resistor [tolerance=±5% resistance=330 package=THT]
  R8 = Resistor [tolerance=±5% resistance=330 package=THT]
  RE1 = Rotary Encoder [package=THT]
  RE2 = Rotary Encoder [package=THT]
  R9 = Resistor [tolerance=±20% resistance=1k package=THT]
  TRS1 = Audio Jack (TRS) 3.5mm [package="4Ucon 08780 [THT]"]

nets:
  N1: Parte1.A0, RE2.EncoderPinC
  N2: Parte1.D11_PWM/MOSI, R8.Pin_1
  N3: Parte1.D12/MISO, R7.Pin_1
  N4: Parte1.GND, LED1.cathode, LED2.cathode, RE1.EncoderPinA, RE2.EncoderPinB, TRS1.Sleeve
  N5: Parte1.D2, R3.Pin_1
  N6: Parte1.D3_PWM, R1.Pin_1
  N7: Parte1.D4, R5.Pin_1
  N8: Parte1.D5_PWM, R4.Pin_1
  N9: Parte1.D6_PWM, R6.Pin_1
  N10: Parte1.5V, RE2.EncoderPinA
  N11: R1.Pin_0, R4.Pin_0, R5.Pin_0, R3.Pin_0, R6.Pin_0, RE1.EncoderPinB
  N12: LED1.anode, R7.Pin_0
  N13: LED2.anode, R8.Pin_0
  N14: RE1.EncoderPinC, R9.Pin_1
  N15: R9.Pin_0, TRS1.Ring, TRS1.Tip

notes:
  volume
  tempo setting
  passive audio mixing
  tempo
  sound
